// Logisim project aialu.circ as structural Verilog
module and_8_bits (
  input  [7:0] A,
  input  [7:0] B,
  output [7:0] out_3,
  output out_4
);

  half_adder half_adder_1 (
    .A(A), .B(B), .out_3(out_3[7]), .out_4(out_3[6]), .out_5(out_3[5]), .out_6(out_3[4]), .out_7(out_3[3]),
    .out_8(out_3[2]), .out_9(out_3[1]), .out_10(out_3[0]), .out_11(out_4));
endmodule

module half_adder (
  input  [7:0] A,
  input  [7:0] B,
  output out_3,
  output out_4,
  output out_5,
  output out_6,
  output out_7,
  output out_8,
  output out_9,
  output out_10,
  output out_11
);

  wire f_a_2_c_2, f_a_3_c_2, f_a_4_c_2, f_a_5_c_2, f_a_6_c_2, f_a_7_c_2, h_a_1_c;

  f_a f_a_1 (.a(A[7]), .b(B[7]), .c(f_a_2_c_2), .s(out_3), .c_2(out_11));
  f_a f_a_2 (.a(A[6]), .b(B[6]), .c(f_a_3_c_2), .s(out_4), .c_2(f_a_2_c_2));
  f_a f_a_3 (.a(A[5]), .b(B[5]), .c(f_a_4_c_2), .s(out_5), .c_2(f_a_3_c_2));
  f_a f_a_4 (.a(A[4]), .b(B[4]), .c(f_a_5_c_2), .s(out_6), .c_2(f_a_4_c_2));
  f_a f_a_5 (.a(A[3]), .b(B[3]), .c(f_a_6_c_2), .s(out_7), .c_2(f_a_5_c_2));
  f_a f_a_6 (.a(A[2]), .b(B[2]), .c(f_a_7_c_2), .s(out_8), .c_2(f_a_6_c_2));
  f_a f_a_7 (.a(A[1]), .b(B[1]), .c(h_a_1_c), .s(out_9), .c_2(f_a_7_c_2));
  h_a h_a_1 (.a(A[0]), .b(B[0]), .s(out_10), .c(h_a_1_c));
endmodule

module h_a (
  input  a,
  input  b,
  output s,
  output c
);

  wire and_2_out, and_3_out, not_1_out, not_2_out;

  not not_1 (not_1_out, a);
  not not_2 (not_2_out, b);
  and and_1 (c, a, b);
  and and_2 (and_2_out, not_1_out, b);
  and and_3 (and_3_out, a, not_2_out);
  or or_1 (s, and_2_out, and_3_out);
endmodule

module f_a (
  input  a,
  input  b,
  input  c,
  output s,
  output c_2
);

  wire and_1_out, and_2_out, and_3_out, and_4_out, and_5_out, and_6_out, and_7_out, not_1_out, not_2_out,
       not_3_out, not_4_out, not_5_out, not_6_out;

  not not_1 (not_1_out, a);
  not not_2 (not_2_out, b);
  not not_3 (not_3_out, a);
  not not_4 (not_4_out, c);
  not not_5 (not_5_out, b);
  not not_6 (not_6_out, c);
  and and_1 (and_1_out, b, c);
  and and_2 (and_2_out, a, c);
  and and_3 (and_3_out, a, b);
  and and_4 (and_4_out, not_1_out, not_2_out, c);
  and and_5 (and_5_out, not_3_out, b, not_4_out);
  and and_6 (and_6_out, a, not_5_out, not_6_out);
  and and_7 (and_7_out, a, b, c);
  or or_1 (c_2, and_1_out, and_2_out, and_3_out);
  or or_2 (s, and_4_out, and_5_out, and_6_out, and_7_out);
endmodule
